// Logisim project 16 bit register controller.circ as structural Verilog: 1 circuit, main circuit main
module main (
  input  in_1,
  input  [15:0] in_2
);

  wire clock_1_out;
  wire [2:0] counter_1_q;
  wire [6:0] rom_1_data;
  wire [15:0] multiplexer_1_out, register_1_q, register_2_q, register_3_q, register_4_q;

  Multiplexer #(.select(3), .width(16)) multiplexer_1 (
    .in0(in_2), .in1(register_1_q), .in2(register_2_q), .in3(register_3_q), .in4(register_4_q),
    .in5({16{1'b0}}), .in6({16{1'b0}}), .in7({16{1'b0}}), .out(multiplexer_1_out), .sel(rom_1_data[6:4]));  // open: en
  Clock clock_1 (.out(clock_1_out));
  Counter #(.width(3), .max('h7)) counter_1 (
    .Q(counter_1_q), .clk(clock_1_out), .clr(in_1));  // open: load, D, count, carry
  Register #(.width(16)) register_1 (
    .D(multiplexer_1_out), .en(rom_1_data[3]), .Q(register_1_q), .clk(clock_1_out));  // open: clr
  ROM #(.addrWidth(3), .dataWidth(7)) rom_1 (.addr(counter_1_q), .data(rom_1_data), .sel(1'b1));
  Register #(.width(16)) register_2 (
    .D(multiplexer_1_out), .en(rom_1_data[2]), .Q(register_2_q), .clk(clock_1_out));  // open: clr
  Register #(.width(16)) register_3 (
    .D(multiplexer_1_out), .en(rom_1_data[1]), .Q(register_3_q), .clk(clock_1_out));  // open: clr
  Register #(.width(16)) register_4 (
    .D(multiplexer_1_out), .en(rom_1_data[0]), .Q(register_4_q), .clk(clock_1_out));  // open: clr

  // Notes on the sheet:
  //   A
  //   contents of rom_1 (hex, n*v repeats v):
  //   8 14 21 42
  //   B
  //      C
  //   D
endmodule
