// Logisim project 16_bit_ALU_adib105.circ as structural Verilog: 10 circuits, main circuit main
module main (
  input  [15:0] in_1,
  input  [15:0] in_2,
  input  in_3,
  input  Control1,
  output [15:0] out_5,
  output Zero,
  output Negative,
  output Carry,
  output Overflow
);

  _16_bit_ALU u_16_bit_alu_1 (
    .in_1(in_1), .in_2(in_2), .Control0(in_3), .Control1(Control1), .out_5(out_5), .Zero(Zero),
    .Negative(Negative), .Carry(Carry), .Overflow(Overflow));

  // Notes on the sheet:
  //   A
  //   B
  //   Control0
  //   16 bit ALU
  //   Result
endmodule

module _16_bit_AND (
  input  [15:0] in_1,
  input  [15:0] in_2,
  output [15:0] out_3
);

  and and_1 (out_3[0], in_1[0], in_2[0]);
  and and_2 (out_3[1], in_1[1], in_2[1]);
  and and_3 (out_3[2], in_1[2], in_2[2]);
  and and_4 (out_3[3], in_1[3], in_2[3]);
  and and_5 (out_3[4], in_1[4], in_2[4]);
  and and_6 (out_3[5], in_1[5], in_2[5]);
  and and_7 (out_3[6], in_1[6], in_2[6]);
  and and_8 (out_3[7], in_1[7], in_2[7]);
  and and_9 (out_3[8], in_1[8], in_2[8]);
  and and_10 (out_3[9], in_1[9], in_2[9]);
  and and_11 (out_3[10], in_1[10], in_2[10]);
  and and_12 (out_3[11], in_1[11], in_2[11]);
  and and_13 (out_3[12], in_1[12], in_2[12]);
  and and_14 (out_3[13], in_1[13], in_2[13]);
  and and_15 (out_3[14], in_1[14], in_2[14]);
  and and_16 (out_3[15], in_1[15], in_2[15]);
endmodule

module _16_bit_OR (
  input  [15:0] in_1,
  input  [15:0] in_2,
  output [15:0] out_3
);

  or or_1 (out_3[0], in_1[0], in_2[0]);
  or or_2 (out_3[1], in_1[1], in_2[1]);
  or or_3 (out_3[2], in_1[2], in_2[2]);
  or or_4 (out_3[3], in_1[3], in_2[3]);
  or or_5 (out_3[4], in_1[4], in_2[4]);
  or or_6 (out_3[5], in_1[5], in_2[5]);
  or or_7 (out_3[6], in_1[6], in_2[6]);
  or or_8 (out_3[7], in_1[7], in_2[7]);
  or or_9 (out_3[8], in_1[8], in_2[8]);
  or or_10 (out_3[9], in_1[9], in_2[9]);
  or or_11 (out_3[10], in_1[10], in_2[10]);
  or or_12 (out_3[11], in_1[11], in_2[11]);
  or or_13 (out_3[12], in_1[12], in_2[12]);
  or or_14 (out_3[13], in_1[13], in_2[13]);
  or or_15 (out_3[14], in_1[14], in_2[14]);
  or or_16 (out_3[15], in_1[15], in_2[15]);
endmodule

module _16_bit_XOR (
  input  in_1,
  input  [15:0] in_2,
  output [15:0] out_3
);

  wire [15:0] bit_extender_1_out;

  assign bit_extender_1_out = {{15{in_1}}, in_1};  // Bit_Extender bit_extender_1
  xor xor_1 (out_3[0], bit_extender_1_out[0], in_2[0]);
  xor xor_2 (out_3[1], bit_extender_1_out[1], in_2[1]);
  xor xor_3 (out_3[2], bit_extender_1_out[2], in_2[2]);
  xor xor_4 (out_3[3], bit_extender_1_out[3], in_2[3]);
  xor xor_5 (out_3[4], bit_extender_1_out[4], in_2[4]);
  xor xor_6 (out_3[5], bit_extender_1_out[5], in_2[5]);
  xor xor_7 (out_3[6], bit_extender_1_out[6], in_2[6]);
  xor xor_8 (out_3[7], bit_extender_1_out[7], in_2[7]);
  xor xor_9 (out_3[8], bit_extender_1_out[8], in_2[8]);
  xor xor_10 (out_3[9], bit_extender_1_out[9], in_2[9]);
  xor xor_11 (out_3[10], bit_extender_1_out[10], in_2[10]);
  xor xor_12 (out_3[11], bit_extender_1_out[11], in_2[11]);
  xor xor_13 (out_3[12], bit_extender_1_out[12], in_2[12]);
  xor xor_14 (out_3[13], bit_extender_1_out[13], in_2[13]);
  xor xor_15 (out_3[14], bit_extender_1_out[14], in_2[14]);
  xor xor_16 (out_3[15], bit_extender_1_out[15], in_2[15]);
endmodule

module full_adder_1bit (
  input  Cin,
  input  A,
  input  B,
  output S,
  output C
);

  wire and_1_out, and_2_out, xor_1_out;

  xor xor_1 (xor_1_out, A, B);
  and and_1 (and_1_out, xor_1_out, Cin);
  and and_2 (and_2_out, A, B);
  xor xor_2 (S, xor_1_out, Cin);
  or or_1 (C, and_1_out, and_2_out);
endmodule

module full_adder_16_bit (
  input  in_1,
  input  [15:0] in_2,
  input  [15:0] in_3,
  output [15:0] out_4,
  output out_5
);

  wire full_adder_1bit_1_c, full_adder_1bit_2_c, full_adder_1bit_3_c, full_adder_1bit_4_c,
       full_adder_1bit_6_c, full_adder_1bit_7_c, full_adder_1bit_8_c, full_adder_1bit_9_c,
       full_adder_1bit_10_c, full_adder_1bit_11_c, full_adder_1bit_12_c, full_adder_1bit_13_c,
       full_adder_1bit_14_c, full_adder_1bit_15_c, full_adder_1bit_16_c;

  full_adder_1bit full_adder_1bit_1 (
    .Cin(full_adder_1bit_16_c), .A(in_2[11]), .B(in_3[11]), .S(out_4[11]), .C(full_adder_1bit_1_c));
  full_adder_1bit full_adder_1bit_2 (
    .Cin(full_adder_1bit_1_c), .A(in_2[12]), .B(in_3[12]), .S(out_4[12]), .C(full_adder_1bit_2_c));
  full_adder_1bit full_adder_1bit_3 (
    .Cin(full_adder_1bit_2_c), .A(in_2[13]), .B(in_3[13]), .S(out_4[13]), .C(full_adder_1bit_3_c));
  full_adder_1bit full_adder_1bit_4 (
    .Cin(full_adder_1bit_3_c), .A(in_2[14]), .B(in_3[14]), .S(out_4[14]), .C(full_adder_1bit_4_c));
  full_adder_1bit full_adder_1bit_5 (.Cin(full_adder_1bit_4_c), .A(in_2[15]), .B(in_3[15]), .S(out_4[15]), .C(out_5));
  full_adder_1bit full_adder_1bit_6 (.Cin(in_1), .A(in_2[0]), .B(in_3[0]), .S(out_4[0]), .C(full_adder_1bit_6_c));
  full_adder_1bit full_adder_1bit_7 (
    .Cin(full_adder_1bit_6_c), .A(in_2[1]), .B(in_3[1]), .S(out_4[1]), .C(full_adder_1bit_7_c));
  full_adder_1bit full_adder_1bit_8 (
    .Cin(full_adder_1bit_7_c), .A(in_2[2]), .B(in_3[2]), .S(out_4[2]), .C(full_adder_1bit_8_c));
  full_adder_1bit full_adder_1bit_9 (
    .Cin(full_adder_1bit_8_c), .A(in_2[3]), .B(in_3[3]), .S(out_4[3]), .C(full_adder_1bit_9_c));
  full_adder_1bit full_adder_1bit_10 (
    .Cin(full_adder_1bit_9_c), .A(in_2[4]), .B(in_3[4]), .S(out_4[4]), .C(full_adder_1bit_10_c));
  full_adder_1bit full_adder_1bit_11 (
    .Cin(full_adder_1bit_10_c), .A(in_2[5]), .B(in_3[5]), .S(out_4[5]), .C(full_adder_1bit_11_c));
  full_adder_1bit full_adder_1bit_12 (
    .Cin(full_adder_1bit_11_c), .A(in_2[6]), .B(in_3[6]), .S(out_4[6]), .C(full_adder_1bit_12_c));
  full_adder_1bit full_adder_1bit_13 (
    .Cin(full_adder_1bit_12_c), .A(in_2[7]), .B(in_3[7]), .S(out_4[7]), .C(full_adder_1bit_13_c));
  full_adder_1bit full_adder_1bit_14 (
    .Cin(full_adder_1bit_13_c), .A(in_2[8]), .B(in_3[8]), .S(out_4[8]), .C(full_adder_1bit_14_c));
  full_adder_1bit full_adder_1bit_15 (
    .Cin(full_adder_1bit_14_c), .A(in_2[9]), .B(in_3[9]), .S(out_4[9]), .C(full_adder_1bit_15_c));
  full_adder_1bit full_adder_1bit_16 (
    .Cin(full_adder_1bit_15_c), .A(in_2[10]), .B(in_3[10]), .S(out_4[10]), .C(full_adder_1bit_16_c));
endmodule

module _15th_bit_out (
  input  [15:0] in_1,
  output out_2
);


  assign out_2 = in_1[15];
endmodule

module adder_subtractor_16bit (
  input  Sub_or_Add,
  input  [15:0] in_2,
  input  [15:0] in_3,
  output [15:0] out_4,
  output Cout,
  output overflow
);

  wire and_1_out, and_2_out, n15th_bit_out_1_out_2, n15th_bit_out_2_out_2, n15th_bit_out_3_out_2, not_1_out,
       not_2_out, not_3_out;
  wire [15:0] n16_bit_xor_1_out_3;

  _15th_bit_out u_15th_bit_out_1 (.in_1(in_2), .out_2(n15th_bit_out_1_out_2));
  _15th_bit_out u_15th_bit_out_2 (.in_1(in_3), .out_2(n15th_bit_out_2_out_2));
  _16_bit_XOR u_16_bit_xor_1 (.in_1(Sub_or_Add), .in_2(in_3), .out_3(n16_bit_xor_1_out_3));
  full_adder_16_bit full_adder_16_bit_1 (
    .in_1(Sub_or_Add), .in_2(in_2), .in_3(n16_bit_xor_1_out_3), .out_4(out_4), .out_5(Cout));
  not not_1 (not_1_out, n15th_bit_out_1_out_2);
  not not_2 (not_2_out, n15th_bit_out_2_out_2);
  _15th_bit_out u_15th_bit_out_3 (.in_1(out_4), .out_2(n15th_bit_out_3_out_2));
  not not_3 (not_3_out, n15th_bit_out_3_out_2);
  and and_1 (and_1_out, n15th_bit_out_3_out_2, not_1_out, not_2_out);
  and and_2 (and_2_out, not_3_out, n15th_bit_out_1_out_2, n15th_bit_out_2_out_2);
  or or_1 (overflow, and_1_out, and_2_out);

  // Notes on the sheet:
  //   A
  //   B
  //   MSB of A
  //   MSB of B
  //   16 bit xor
  //   16 bit adder
  //   MSB of result
  //   Result
endmodule

module _16bit_reduced_or (
  input  [15:0] in_1,
  output out_2
);

  or or_1 (out_2, in_1[0], in_1[1], in_1[2], in_1[3], in_1[4], in_1[5], in_1[6], in_1[7], in_1[8], in_1[9], in_1[10], in_1[11], in_1[12], in_1[13], in_1[14], in_1[15]);
endmodule

module _16_bit_ALU (
  input  [15:0] in_1,
  input  [15:0] in_2,
  input  Control0,
  input  Control1,
  output [15:0] out_5,
  output Zero,
  output Negative,
  output Carry,
  output Overflow
);

  wire n16bit_reduced_or_1_out_2;
  wire [15:0] adder_subtractor_16bit_1_out_4, multiplexer_1_out, n16_bit_and_1_out_3, n16_bit_or_1_out_3;

  _16_bit_AND u_16_bit_and_1 (.in_1(in_1), .in_2(in_2), .out_3(n16_bit_and_1_out_3));
  _16_bit_OR u_16_bit_or_1 (.in_1(in_1), .in_2(in_2), .out_3(n16_bit_or_1_out_3));
  adder_subtractor_16bit adder_subtractor_16bit_1 (
    .Sub_or_Add(Control0), .in_2(in_1), .in_3(in_2), .out_4(adder_subtractor_16bit_1_out_4), .Cout(Carry),
    .overflow(Overflow));
  Multiplexer #(.width(16), .enable("false")) multiplexer_1 (
    .in0(n16_bit_and_1_out_3), .in1(n16_bit_or_1_out_3), .out(multiplexer_1_out), .sel(Control0));
  Multiplexer #(.width(16), .enable("false")) multiplexer_2 (
    .in0(multiplexer_1_out), .in1(adder_subtractor_16bit_1_out_4), .out(out_5), .sel(Control1));
  _16bit_reduced_or u_16bit_reduced_or_1 (.in_1(out_5), .out_2(n16bit_reduced_or_1_out_2));
  not not_1 (Zero, n16bit_reduced_or_1_out_2);
  _15th_bit_out u_15th_bit_out_1 (.in_1(out_5), .out_2(Negative));

  // Notes on the sheet:
  //   A
  //   B
  //   16 bit AND
  //   16 bit OR
  //   ADD / SUB 16 bit
  //   Result
endmodule
